# Fritzing sketch Smart Agriculture System (saved by Fritzing 0.9.3b)
breadboards: 1

parts:
  부품1 = FC-28 Soil Hygrometer Module - Probe
  부품2 = FC-28 Soil Hygrometer Module
  U1 = ESP32-38PinWide [part_number=ESP32-38PinWide]
  DHT1 = DHT11 Humitidy and Temperature Sensor
  Water_Level_Sensor1 = Water Level Sensor
  KY-1 = Keyes Relay [package=THT]

nets:
  N1: 부품1.POS, 부품2.POS
  N2: 부품1.NEG, 부품2.NEG
  VCC: 부품2.VCC, U1.3.3, DHT1.VDD, Water_Level_Sensor1.VCC, KY-1.power
  GND: 부품2.GND, U1.GND, DHT1.DATA, DHT1.GND, Water_Level_Sensor1.GND, KY-1.ground
  N3: 부품2.AO, U1.GPIO15
  N4: U1.GPIO2, Water_Level_Sensor1.SIG
  N5: U1.GPIO3, U1.GPIO1
  N6: U1.GPIO23, KY-1.signal

notes:
  Wire Key
  POWER
  Ground
  DHT11 INPUT
  SOIL SENSOR INPUT
  WATER SENSOR INPUT
  RELAY
  BLACK
  Green
  YELLOW
  ORANGE
  BLUE
  RED

custom parts:
  FC-28 Soil Hygrometer Module - Probe: The FC-28 is a soil hygrometer module that uses the Texas Instruments LM393 comparator chip to provide an analog measurement of soil humidity.
  FC-28 Soil Hygrometer Module: The FC-28 is a soil hygrometer module that uses the Texas Instruments LM393 comparator chip to provide an analog measurement of soil humidity. The digital output is high when soil moisture is over a certain threshold, as determined by adjusting the potentiometer.
  ESP32-38PinWide: Generic 38-Pin ESP32 with wide format (only access to one side of pins on a breadboard) based on Stephen Lilley's HiLetgo ESP-WROOM-32 ESP32 ESP-32S Development Board.
  DHT11 Humitidy and Temperature Sensor: DHT11 Humidity and Temperature Sensor
  Water Level Sensor: A water level sensor. This sensor operates at 3V to 5V. The Sig (signal) pin outputs an analogue signal that is in proportion to the amount of water in contact with the sensor.
  Keyes Relay: The Keyes 5V relay module is suitable for SCM development, home appliance control. It uses a 5V~12V TIL control signal which can control DC / AC signal.
